# Fritzing sketch diagram (saved by Fritzing 0.9.5d)

parts:
  Part1 = Arduino Uno (Rev3)
  HC-SR04_Sensor_1 = HC-SR04 Ultrasonic Distance Sensor
  S1 = H-Bridge with L298N

nets:
  N1: Part1.D9_PWM, S1.ENA
  N2: Part1.D12/MISO, HC-SR04_Sensor_1.ECHO
  N3: Part1.D13/SCK, HC-SR04_Sensor_1.TRIG
  N4: Part1.D3_PWM, S1.ENB
  N5: Part1.D4, S1.IN4
  N6: Part1.D5_PWM, S1.IN3
  N7: Part1.D6_PWM, S1.IN2
  N8: Part1.D7, S1.IN1
  5V: Part1.5V, HC-SR04_Sensor_1.VCC
  GND: Part1.GND, HC-SR04_Sensor_1.GND, S1.GND
  VIN: Part1.VIN, S1.12V

custom parts:
  H-Bridge with L298N: h-bridge
